// Logisim project proccessor.circ as structural Verilog
module HALF_ADDER (
  input  A,
  input  B,
  output SUM,
  output CARRY
);

  xor xor_1 (SUM, A, B);
  and and_1 (CARRY, A, B);
endmodule

module INC_4BIT (
  input  A,
  input  A_1,
  input  A_2,
  input  A_3,
  input  INC,
  output Y,
  output Y_1,
  output Y_2,
  output Y_3,
  output CARRY
);

  wire half_adder_1_carry, half_adder_2_carry, half_adder_3_carry;

  HALF_ADDER half_adder_1 (.A(INC), .B(A), .SUM(Y), .CARRY(half_adder_1_carry));
  HALF_ADDER half_adder_2 (.A(half_adder_1_carry), .B(A_1), .SUM(Y_1), .CARRY(half_adder_2_carry));
  HALF_ADDER half_adder_3 (.A(half_adder_2_carry), .B(A_2), .SUM(Y_2), .CARRY(half_adder_3_carry));
  HALF_ADDER half_adder_4 (.A(half_adder_3_carry), .B(A_3), .SUM(Y_3), .CARRY(CARRY));
endmodule

module tows_comp (
  input  A,
  input  A_1,
  input  A_2,
  input  A_3,
  output Y,
  output Y_1,
  output Y_2,
  output Y_3,
  output CARRY
);

  wire not_1_out, not_2_out, not_3_out, not_4_out;

  not not_1 (not_1_out, A);
  not not_2 (not_2_out, A_1);
  not not_3 (not_3_out, A_2);
  not not_4 (not_4_out, A_3);
  INC_4BIT inc_4bit_1 (
    .A(not_1_out), .A_1(not_2_out), .A_2(not_3_out), .A_3(not_4_out), .INC(1'b1), .Y(Y), .Y_1(Y_1),
    .Y_2(Y_2), .Y_3(Y_3), .CARRY(CARRY));
endmodule

module FULL_ADDER_1BIT (
  input  A,
  input  B,
  input  CARRY_IN,
  output SUM,
  output CARRY_OUT
);

  wire or_1_out, or_2_out, or_3_out;

  or or_1 (or_1_out, CARRY_IN, B);
  or or_2 (or_2_out, CARRY_IN, A);
  or or_3 (or_3_out, B, A);
  xor xor_1 (SUM, A, B, CARRY_IN);
  and and_1 (CARRY_OUT, or_1_out, or_2_out, or_3_out);
endmodule
